// Digital circuit LAB2_cs303.dig as structural Verilog
module LAB2_cs303 (
  input  X1,
  input  X0,
  input  Y1,
  input  Y0,
  output A1,
  output A0
);

  wire and_1_out, and_2_out, and_3_out, and_4_out, not_1_out, not_2_out, not_3_out, not_4_out, or_1_out,
       or_2_out;

  not not_1 (not_1_out, X1);
  not not_2 (not_2_out, X0);
  not not_3 (not_3_out, Y0);
  not not_4 (not_4_out, Y1);
  and and_1 (and_1_out, not_1_out, X0, Y1);
  and and_2 (and_2_out, X1, not_2_out, Y0);
  and and_3 (and_3_out, X0, not_3_out, Y1);
  and and_4 (and_4_out, X1, Y0, not_4_out);
  and and_5 (A0, X0, Y0);
  or or_1 (or_1_out, and_1_out, and_2_out);
  or or_2 (or_2_out, and_3_out, and_4_out);
  or or_3 (A1, or_1_out, or_2_out);
endmodule
